// Digital circuit CPU_RISCV.dig as structural Verilog
module CPU_RISCV (
  input  clk,
  input  [31:0] SysInput,
  input  in_3
);

  wire not_1_out, u_ALU_Decoder_branch_cond, u_BubbleUnit_hold_sig, u_MainCtrl_alusrc, u_MainCtrl_branch,
       u_MainCtrl_jumpreg, u_MainCtrl_memread, u_MainCtrl_regwrite, u_PipeReg_EX_MEM_branch,
       u_PipeReg_EX_MEM_regwrite, u_PipeReg_ID_EX_branch, u_PipeReg_ID_EX_memread, u_PipeReg_ID_EX_memtoreg,
       u_PipeReg_ID_EX_regwrite, u_PipeReg_MEM_WB_regwrite, undriven_6, undriven_7, undriven_9, undriven_10,
       undriven_11, undriven_16, undriven_17, undriven_18, undriven_19, undriven_20, undriven_30,
       undriven_32, undriven_35, undriven_36, undriven_40, undriven_42, undriven_43, undriven_46, undriven_48;
  wire [1:0] u_BypassUnit_fwdmuxa, u_BypassUnit_fwdmuxb;
  wire [2:0] u_PipeReg_ID_EX_funct3;
  wire [3:0] u_ALU_Decoder_alu_control, undriven_29;
  wire [4:0] u_FetchStage_rd_addr, u_FetchStage_rs1_addr, u_FetchStage_rs2_addr, u_PipeReg_EX_MEM_rd,
       undriven_3, undriven_31, undriven_39, undriven_44;
  wire [6:0] u_MainCtrl_funct7, u_PipeReg_ID_EX_funct7;
  wire [15:0] ramdualport_1_d, ramdualport_2_d, u_AddrUnpacker_unpacked_high, u_AddrUnpacker_unpacked_low,
       u_DataUnpacker_unpacked_high, u_DataUnpacker_unpacked_low, undriven_5, undriven_8, undriven_12,
       undriven_13;
  wire [31:0] GPR_Block_da, multiplexer_1_out, multiplexer_2_out, multiplexer_3_out, multiplexer_4_out,
       multiplexer_5_out, multiplexer_8_out, u_Adder32_resultsum, u_DataPacker_packed_out,
       u_PipeReg_EX_MEM_pc2, u_PipeReg_EX_MEM_regdatab, u_PipeReg_ID_EX_imm, u_PipeReg_ID_EX_pc,
       u_PipeReg_ID_EX_regdataa, u_PipeReg_ID_EX_regdatab, undriven, undriven_2, undriven_4, undriven_14,
       undriven_15, undriven_21, undriven_22, undriven_23, undriven_24, undriven_25, undriven_26,
       undriven_27, undriven_28, undriven_33, undriven_34, undriven_37, undriven_38, undriven_41,
       undriven_45, undriven_47, undriven_49;

  Multiplexer #(.Bits(32)) multiplexer_1 (.in_1(undriven_49), .out(multiplexer_1_out));  // open: sel, in_0
  ProgCounter #(.applicationType("GHDL"), .CodeFile("C:\\Projetos\\riscv_core\\rtl\\PC.vhd")) u_ProgCounter (
    .addr_in(multiplexer_1_out), .w_en(undriven_48));  // open: clock, rst_n, addr_out
  FetchStage #(.applicationType("GHDL"), .CodeFile("C:\\Projetos\\riscv_core\\rtl\\instr_fetch.vhd")) u_FetchStage (
    .next_addr_in(undriven_47), .raw_instr(undriven_45), .rs1_addr(u_FetchStage_rs1_addr),
    .rs2_addr(u_FetchStage_rs2_addr), .rd_addr(u_FetchStage_rd_addr));  // open: clock, w_en, addr_in, addr_out, next_addr_out, fetched_instr
  BubbleUnit #(.applicationType("GHDL"), .CodeFile("C:\\Projetos\\riscv_core\\rtl\\Hazard.vhd")) u_BubbleUnit (
    .clock(undriven_46), .MemRead(undriven_43), .rs1_addr(undriven_44), .hold_sig(u_BubbleUnit_hold_sig));  // open: rs2_addr, rd_addr
  not not_1 (not_1_out, undriven_42);
  MainCtrl #(.applicationType("GHDL"), .CodeFile("C:\\Projetos\\riscv_core\\rtl\\Control.vhd")) u_MainCtrl (
    .op_code_word(undriven_41), .hold_sig(u_BubbleUnit_hold_sig), .Branch(u_MainCtrl_branch),
    .MemRead(u_MainCtrl_memread), .ALUsrc(u_MainCtrl_alusrc), .RegWrite(u_MainCtrl_regwrite),
    .funct7(u_MainCtrl_funct7), .JumpReg(u_MainCtrl_jumpreg));  // open: MemtoReg, ALUop, MemWrite, funct3, opcode, PC_shift_ctrl
  RegisterFile #(.AddrBits(5), .Bits(32)) GPR_Block (
    .Din(undriven_38), .Ra(u_FetchStage_rs1_addr), .Rb(u_FetchStage_rs2_addr), .Da(GPR_Block_da));  // open: we, Rw, C, Db
  ImmExtender #(.applicationType("GHDL"), .CodeFile("C:\\Projetos\\riscv_core\\rtl\\ImmGen.vhd")) u_ImmExtender ();  // open: instruction, extended_imm
  PipeReg_ID_EX #(.applicationType("GHDL"), .CodeFile("C:\\Projetos\\riscv_core\\rtl\\idex.vhd")) u_PipeReg_ID_EX (
    .clock(undriven_36), .Branch_in(u_MainCtrl_branch), .MemRead_in(u_MainCtrl_memread),
    .ALUscr_in(u_MainCtrl_alusrc), .RegWrite_in(u_MainCtrl_regwrite), .funct7_in(u_MainCtrl_funct7),
    .JumpReg_in(u_MainCtrl_jumpreg), .PC_in(undriven_37), .RegDataA_in(undriven_34),
    .RegDataB_in(undriven_33), .rd_in(undriven_39), .Branch(u_PipeReg_ID_EX_branch),
    .MemRead(u_PipeReg_ID_EX_memread), .MemtoReg(u_PipeReg_ID_EX_memtoreg),
    .RegWrite(u_PipeReg_ID_EX_regwrite), .funct7(u_PipeReg_ID_EX_funct7), .funct3(u_PipeReg_ID_EX_funct3),
    .PC(u_PipeReg_ID_EX_pc), .RegDataA(u_PipeReg_ID_EX_regdataa), .RegDataB(u_PipeReg_ID_EX_regdatab),
    .imm(u_PipeReg_ID_EX_imm));  // open: MemtoReg_in, ALUop_in, MemWrite_in, funct3_in, opcode_in, PC_shift_ctrl_in, imm_in, rs1_in, rs2_in, ALUop, MemWrite, ALUscr, opcode, PC_shift_ctrl, JumpReg, rs1, rs2, rd
  BypassUnit #(.applicationType("GHDL"), .CodeFile("C:\\Projetos\\riscv_core\\rtl\\Forward.vhd")) u_BypassUnit (
    .clock(undriven_40), .WB_RegWrite(undriven_35), .MEM_RegWrite(undriven_32), .MEM_rd(undriven_31),
    .FwdMuxA(u_BypassUnit_fwdmuxa), .FwdMuxB(u_BypassUnit_fwdmuxb));  // open: rs1_addr, rs2_addr, WB_rd
  ALU_Decoder #(.applicationType("GHDL"), .CodeFile("C:\\Projetos\\riscv_core\\rtl\\ULA_control.vhd")) u_ALU_Decoder (
    .funct7(u_PipeReg_ID_EX_funct7), .funct3(u_PipeReg_ID_EX_funct3),
    .alu_control(u_ALU_Decoder_alu_control), .branch_cond(u_ALU_Decoder_branch_cond));  // open: opcode, ALUop
  // And and_1 has open pins: In_1=open, In_2=undriven_30, out=open
  Multiplexer #(.Bits(32)) multiplexer_2 (.in_1(undriven_27), .out(multiplexer_2_out));  // open: sel, in_0
  Multiplexer #(.Bits(32)) multiplexer_3 (.in_1(undriven_26), .out(multiplexer_3_out));  // open: sel, in_0
  Multiplexer #(.Bits(32)) multiplexer_4 (.in_0(undriven_28), .out(multiplexer_4_out));  // open: sel, in_1
  Multiplexer #(.Bits(32)) multiplexer_5 (
    .in_0(multiplexer_2_out), .in_1(undriven_25), .out(multiplexer_5_out));  // open: sel
  Adder32 #(.applicationType("GHDL"), .CodeFile("C:\\Projetos\\riscv_core\\rtl\\adder.vhd")) u_Adder32 (
    .OperandA(multiplexer_3_out), .OperandB(undriven_24), .ResultSum(u_Adder32_resultsum));
  Multiplexer #(.Selector_Bits(2), .Bits(32)) multiplexer_6 (
    .in_0(multiplexer_5_out), .in_1(undriven_23));  // open: sel, in_2, in_3, out
  Multiplexer #(.Selector_Bits(2), .Bits(32)) multiplexer_7 (.in_0(multiplexer_4_out));  // open: sel, in_1, in_2, in_3, out
  ALU_Unit #(.applicationType("GHDL"), .CodeFile("C:\\Projetos\\riscv_core\\rtl\\ULA.vhd")) u_ALU_Unit (.alu_control(undriven_29));  // open: SrcMuxA, SrcMuxB, alu_out, zero_flag
  // And and_2 is placed but not wired
  PipeReg_EX_MEM #(.applicationType("GHDL"), .CodeFile("C:\\Projetos\\riscv_core\\rtl\\exmem.vhd")) u_PipeReg_EX_MEM (
    .clock(undriven_18), .MemWrite_in(undriven_19), .RegWrite_in(undriven_20), .PC2_in(undriven_21),
    .RegDataB_in(undriven_22), .jar_in(undriven_17), .Branch(u_PipeReg_EX_MEM_branch),
    .RegWrite(u_PipeReg_EX_MEM_regwrite), .PC2(u_PipeReg_EX_MEM_pc2), .RegDataB(u_PipeReg_EX_MEM_regdatab),
    .rd(u_PipeReg_EX_MEM_rd));  // open: Branch_in, MemRead_in, MemtoReg_in, rd_in, zero_flag_in, alu_out_in, MemRead, MemtoReg, MemWrite, zero_flag, alu_out, jar
  // And and_3 is placed but not wired
  // Or or_1 has open pins: In_1=open, In_2=undriven_16, out=open
  DataUnpacker #(.applicationType("GHDL"), .CodeFile("C:\\Projetos\\riscv_core\\rtl\\spliter.vhd")) u_DataUnpacker (
    .packed_32(undriven_14), .unpacked_high(u_DataUnpacker_unpacked_high),
    .unpacked_low(u_DataUnpacker_unpacked_low));
  AddrUnpacker #(.applicationType("GHDL"), .CodeFile("C:\\Projetos\\riscv_core\\rtl\\spliter.vhd")) u_AddrUnpacker (
    .packed_32(undriven_15), .unpacked_high(u_AddrUnpacker_unpacked_high),
    .unpacked_low(u_AddrUnpacker_unpacked_low));
  RAMDualPort #(.AddrBits(16), .Bits(16)) ramdualport_1 (
    .A(undriven_13), .Din(undriven_12), .str(undriven_10), .D(ramdualport_1_d));  // open: C, ld
  RAMDualPort #(.AddrBits(16), .Bits(16)) ramdualport_2 (
    .A(u_DataUnpacker_unpacked_low), .Din(undriven_8), .str(undriven_9), .C(undriven_11), .ld(undriven_7),
    .D(ramdualport_2_d));
  DataPacker #(.applicationType("GHDL"), .CodeFile("C:\\Projetos\\riscv_core\\rtl\\joiner.vhd")) u_DataPacker (
    .half_low(undriven_5), .packed_out(u_DataPacker_packed_out));  // open: half_high
  PipeReg_MEM_WB #(.applicationType("GHDL"), .CodeFile("C:\\Projetos\\riscv_core\\rtl\\memwb.vhd")) u_PipeReg_MEM_WB (
    .clock(undriven_6), .alu_out_in(undriven_4), .rd_in(undriven_3), .RegWrite(u_PipeReg_MEM_WB_regwrite));  // open: RegWrite_in, MemtoReg_in, MemData_in, MemtoReg, MemData, alu_out, rd
  Multiplexer #(.Bits(32)) multiplexer_8 (.in_0(undriven_2), .in_1(undriven), .out(multiplexer_8_out));  // open: sel
endmodule
